// Logisim project 原码和补码一位乘法器.circ as structural Verilog: 8 circuits, main circuit 1位全加器（FA）
// 8位无符号一位乘法器
module \_8位无符号数一位乘法器  (
  input  [7:0] X,
  input  [7:0] Y,
  input  RST,
  input  CLK,
  output END,
  output [15:0] \乘积 
);

  wire comparator_1_eq, d_ff_1_q, not_1_out;
  wire [0:0] \n8位串行加法器_1_s ;
  wire [3:0] counter_1_q;
  wire [7:0] multiplexer_1_out, multiplexer_2_out, \n8位串行加法器_1_cout ;

  // Probe on \乘积 [15:8]
  Register #(.width(8), .trigger("rising"), .Select("low")) register_1 (
    .D(\n8位串行加法器_1_cout ), .en(not_1_out), .Q(\乘积 [15:8]), .clk(CLK), .clr(RST));
  \_8位串行加法器  \u_8位串行加法器_1  (
    .X(\乘积 [15:8]), .Y(multiplexer_1_out), .Cin(1'b0), .S({\n8位串行加法器_1_cout [6:0], \n8位串行加法器_1_s [0]}),
    .Cout(\n8位串行加法器_1_cout [7]));  // open: out_6
  Multiplexer #(.select(1), .width(8), .disabled("Z"), .enable("false")) multiplexer_1 (
    .in0({8{1'b0}}), .in1(X), .out(multiplexer_1_out), .sel(\乘积 [0]));
  Multiplexer #(.select(1), .width(8), .disabled("Z"), .enable("false")) multiplexer_2 (
    .in0(Y), .in1({\n8位串行加法器_1_s [0], \乘积 [7:1]}), .out(multiplexer_2_out), .sel(d_ff_1_q));
  // Probe on \乘积 [7:0]
  Register #(.width(8), .trigger("rising"), .Select("low")) Y_2 (
    .D(multiplexer_2_out), .en(not_1_out), .Q(\乘积 [7:0]), .clk(CLK), .clr(RST));
  Counter #(.width(4), .max('hf), .ongoal("wrap"), .trigger("rising"), .behavior("old")) counter_1 (
    .count(not_1_out), .Q(counter_1_q), .clk(CLK), .clr(RST));  // open: load, D, carry, preset
  D_Flip_Flop #(.trigger("rising"), .Pre_Clr_Positions("LEGACY"), .NegatePresetClear("false"), .enable("true"), .NewFFLayout("false")) d_ff_1 (
    .clk(CLK), .D(1'b1), .Q(d_ff_1_q), .reset(RST));  // open: Qn, preset, en
  Comparator #(.width(4), .mode("unsigned")) comparator_1 (
    .a(counter_1_q), .b(4'b1001), .eq(comparator_1_eq));  // open: gt, lt
  not not_1 (not_1_out, comparator_1_eq);
  not not_2 (END, not_1_out);
  // Probe on X
  // Probe on Y
  // Probe on \乘积 

  // Notes on the sheet:
  //   输入引脚区
  //   ∑
  //   功能说明: 8位无符号数一位乘法器                输入：X、Y 为8位无符号数               输出：乘积=X*Y 为16位无符号数
  //   首先设置X、Y值，然后按“复位”按钮，接下去按“CLK”按钮多次，直到“END”指示灯变红，此时观看乘积是不是正确？
  //   8位无符号数一位乘法器
  //   输出引脚区
  //   ×
  //   =
endmodule

module \_8位原码一位乘法器  (
  input  [7:0] X,
  input  [7:0] Y,
  output [15:0] \乘积 
);

  wire CLK, comparator_1_eq, comparator_2_eq, comparator_3_eq, END, RST, S;
  wire [7:0] adder_1_out, adder_2_out, multiplexer_1_out, multiplexer_2_out, not_1_out, not_2_out, \X真值 ,
       \Y真值 ;
  wire [15:0] adder_3_out, multiplexer_3_out, not_3_out, \乘积真值 ;

  // Probe on {1'b0, X[6:0]}
  // Probe on {1'b0, Y[6:0]}
  xor xor_1 (S, X[7], Y[7]);
  Button \u_复位  (.out(RST));
  \_8位无符号数一位乘法器  \u_8位无符号数一位乘法器_1  (
    .X({1'b0, X[6:0]}), .Y({1'b0, Y[6:0]}), .\乘积 (\乘积 ), .RST(RST), .CLK(CLK), .END(END));
  Button u_CLK (.out(CLK));
  // Probe on \乘积 
  assign not_1_out = ~X;  // NOT_Gate not_1, 8 bits wide
  Adder #(.width(8)) adder_1 (.a(not_1_out), .b(8'h1), .out(adder_1_out));  // open: cin, cout
  assign not_2_out = ~Y;  // NOT_Gate not_2, 8 bits wide
  Adder #(.width(8)) adder_2 (.a(not_2_out), .b(8'h1), .out(adder_2_out));  // open: cin, cout
  assign not_3_out = ~{S, \乘积 [14:0]};  // NOT_Gate not_3, 16 bits wide
  Adder #(.width(16)) adder_3 (.a(not_3_out), .b(16'h1), .out(adder_3_out));  // open: cin, cout
  LED #(.active("true")) led_1 (.in(END));
  Multiplexer #(.select(1), .width(8), .disabled("Z"), .enable("false")) multiplexer_1 (
    .in0(X), .in1(adder_1_out), .out(multiplexer_1_out), .sel(X[7]));
  Multiplexer #(.select(1), .width(8), .disabled("Z"), .enable("false")) multiplexer_2 (
    .in0(Y), .in1(adder_2_out), .out(multiplexer_2_out), .sel(Y[7]));
  Multiplexer #(.select(1), .width(16), .disabled("Z"), .enable("false")) multiplexer_3 (
    .in0({S, \乘积 [14:0]}), .in1(adder_3_out), .out(multiplexer_3_out), .sel(S));
  Comparator #(.width(7), .mode("twosComplement")) comparator_1 (
    .a(multiplexer_1_out[6:0]), .b({7{1'b0}}), .eq(comparator_1_eq));  // open: gt, lt
  Comparator #(.width(7), .mode("twosComplement")) comparator_2 (
    .a(multiplexer_2_out[6:0]), .b({7{1'b0}}), .eq(comparator_2_eq));  // open: gt, lt
  Comparator #(.width(15), .mode("twosComplement")) comparator_3 (
    .a(multiplexer_3_out[14:0]), .b({15{1'b0}}), .eq(comparator_3_eq));  // open: gt, lt
  // Probe on \乘积真值 
  Multiplexer #(.select(1), .width(8), .disabled("Z"), .enable("false")) multiplexer_4 (
    .in0({X[7], multiplexer_1_out[6:0]}), .in1({8{1'b0}}), .out(\X真值 ), .sel(comparator_1_eq));
  Multiplexer #(.select(1), .width(8), .disabled("Z"), .enable("false")) multiplexer_5 (
    .in0({Y[7], multiplexer_2_out[6:0]}), .in1({8{1'b0}}), .out(\Y真值 ), .sel(comparator_2_eq));
  Multiplexer #(.select(1), .width(16), .disabled("Z"), .enable("false")) multiplexer_6 (
    .in0({S, multiplexer_3_out[14:0]}), .in1({16{1'b0}}), .out(\乘积真值 ), .sel(comparator_3_eq));
  // Probe on \X真值 
  // Probe on \Y真值 

  // Other names for the same wires on the sheet: Sx = X[7]; Sy = Y[7]; X_t[6:0] = X[6:0]; Y_t[6:0] = Y[6:0]

  // Notes on the sheet:
  //   输入引脚区
  //   功能说明: 8位原码一位乘法器                输入：X、Y为 8位原码               输出：乘积=X*Y 为16位原码
  //   首先设置X、Y值，然后按“复位”按钮，接下去按“CLK”按钮多次，直到“END”指示灯变红，此时观看乘积是不是正确？
  //   8位原码一位乘法器
  //   输出引脚区
  //   ×
  //   =
endmodule

module \_8位补码一位乘法器_简化版  (
  input  [7:0] X,
  input  [7:0] Y,
  output [15:0] \乘积 
);

  wire and_1_out, CLK, comparator_1_eq, comparator_2_eq, d_ff_1_q, END, not_3_out, RST;
  wire [0:0] \n8位串行加法器_1_s_2 ;
  wire [1:1] Yn_1_2_q;
  wire [3:0] counter_1_q;
  wire [7:0] multiplexer_1_out, multiplexer_2_out, \n8位串行加法器_1_s , not_1_out;
  wire [15:0] negator_1_out, \乘积_star ;

  Register #(.width(8), .trigger("rising"), .Select("low")) register (
    .D({{2{\n8位串行加法器_1_s [7]}}, \n8位串行加法器_1_s [5:0]}), .en(not_3_out), .Q(\乘积_star [15:8]), .clk(CLK),
    .clr(RST));
  assign not_1_out = ~X;  // NOT_Gate not_1, 8 bits wide
  // Probe on \乘积_star [15:8]
  Multiplexer #(.select(1), .width(8), .disabled("Z"), .enable("false")) multiplexer_1 (
    .in0(Y), .in1({\n8位串行加法器_1_s_2 [0], \乘积_star [7:1]}), .out(multiplexer_1_out), .sel(d_ff_1_q));
  \_8位串行加法器  \u_8位串行加法器_1  (
    .X(\乘积_star [15:8]), .Y(multiplexer_2_out), .Cin(and_1_out),
    .S({\n8位串行加法器_1_s [7], \n8位串行加法器_1_s [5:0], \n8位串行加法器_1_s_2 [0]}));  // open: Cout, out_6
  Multiplexer #(.select(2), .width(8), .disabled("Z"), .enable("false")) multiplexer_2 (
    .in0({8{1'b0}}), .in1(not_1_out), .in2(X), .in3({8{1'b0}}), .out(multiplexer_2_out),
    .sel({Yn_1_2_q[1], \乘积_star [0]}));
  Button \u_复位  (.out(RST));
  // Probe on \乘积_star [7:0]
  Register #(.width(8), .trigger("rising"), .Select("low")) Y_2 (
    .D(multiplexer_1_out), .en(not_3_out), .Q(\乘积_star [7:0]), .clk(CLK), .clr(RST));
  and and_1 (and_1_out, ~Yn_1_2_q[1], \乘积_star [0]);  // AND_Gate
  Counter #(.width(4), .max('hf), .ongoal("wrap"), .trigger("rising"), .behavior("old")) counter_1 (
    .count(not_3_out), .Q(counter_1_q), .clk(CLK), .clr(RST));  // open: load, D, carry, preset
  // Probe on Yn_1_2_q[1]
  Register #(.width(1), .trigger("rising"), .Select("low")) Yn_1_2 (
    .D(\乘积_star [0]), .en(not_3_out), .Q(Yn_1_2_q[1]), .clk(CLK), .clr(RST));
  Comparator #(.width(4), .mode("unsigned")) comparator_1 (
    .a(counter_1_q), .b(4'b1001), .eq(comparator_1_eq));  // open: gt, lt
  D_Flip_Flop #(.trigger("rising"), .Pre_Clr_Positions("LEGACY"), .NegatePresetClear("false"), .enable("true"), .NewFFLayout("false")) d_ff_1 (
    .clk(CLK), .D(1'b1), .Q(d_ff_1_q), .reset(RST));  // open: Qn, preset, en
  Button \u_时钟  (.out(CLK));
  not not_2 (END, not_3_out);
  not not_3 (not_3_out, comparator_1_eq);
  // Probe on \乘积_star 
  // Probe on \乘积_star 
  LED #(.active("true")) led_1 (.in(END));
  Negator #(.width(16)) negator_1 (.in(\乘积_star ), .out(negator_1_out));
  Comparator #(.width(8), .mode("twosComplement")) comparator_2 (
    .a(X), .b(8'h80), .eq(comparator_2_eq));  // open: gt, lt
  Multiplexer #(.select(1), .width(16), .disabled("Z"), .enable("false")) multiplexer_3 (
    .in0(\乘积_star ), .in1(negator_1_out), .out(\乘积 ), .sel(comparator_2_eq));
  // Probe on X
  // Probe on Y
  // Probe on \乘积 
  // Probe on \乘积 

  // Notes on the sheet:
  //   输入引脚区
  //   功能说明: 8位补码一位乘法器                输入：X、Y 为8位补码               输出：乘积=X*Y 为16位补码
  //   首先设置X、Y值，然后按“复位”按钮，接下去按“CLK”按钮多次，直到“END”指示灯变红，此时观看乘积是不是正确？
  //   8位补码一位乘法器（简化版）
  //   输出引脚区
  //   ×
  //   =
endmodule

module \_8位补码一位乘法器_复杂版  (
  input  [7:0] X,
  input  [7:0] Y,
  output [15:0] \乘积 
);

  wire and_1_out, CLK, comparator_1_eq, d_ff_1_q, END, not_3_out, RST, XYZ, XZ, YZ;
  wire [0:0] \n8位串行加法器_1_s_2 ;
  wire [1:0] PS;
  wire [1:1] Yn_1_2_q;
  wire [3:0] counter_1_q;
  wire [7:0] multiplexer_1_out, multiplexer_2_out, \n8位串行加法器_1_s , not_1_out;
  wire [14:0] PX_star, PY_star;
  wire [15:0] multiplexer_3_out, P_star;
  wire [15:15] negator_1_out, negator_2_out, PX;

  // Probe on X
  Register #(.width(8), .trigger("rising"), .Select("low")) register (
    .D({{2{\n8位串行加法器_1_s [7]}}, \n8位串行加法器_1_s [5:0]}), .en(not_3_out), .Q(P_star[15:8]), .clk(CLK), .clr(RST));
  assign not_1_out = ~X;  // NOT_Gate not_1, 8 bits wide
  // Probe on Y
  // Probe on P_star[15:8]
  Multiplexer #(.select(1), .width(8), .disabled("Z"), .enable("false")) multiplexer_1 (
    .in0(Y), .in1({\n8位串行加法器_1_s_2 [0], P_star[7:1]}), .out(multiplexer_1_out), .sel(d_ff_1_q));
  \_8位串行加法器  \u_8位串行加法器_1  (
    .X(P_star[15:8]), .Y(multiplexer_2_out), .Cin(and_1_out),
    .S({\n8位串行加法器_1_s [7], \n8位串行加法器_1_s [5:0], \n8位串行加法器_1_s_2 [0]}));  // open: Cout, out_6
  Multiplexer #(.select(2), .width(8), .disabled("Z"), .enable("false")) multiplexer_2 (
    .in0({8{1'b0}}), .in1(not_1_out), .in2(X), .in3({8{1'b0}}), .out(multiplexer_2_out),
    .sel({Yn_1_2_q[1], P_star[0]}));
  Button \u_复位  (.out(RST));
  // Probe on P_star[7:0]
  Register #(.width(8), .trigger("rising"), .Select("low")) Y_2 (
    .D(multiplexer_1_out), .en(not_3_out), .Q(P_star[7:0]), .clk(CLK), .clr(RST));
  and and_1 (and_1_out, ~Yn_1_2_q[1], P_star[0]);  // AND_Gate
  Counter #(.width(4), .max('hf), .ongoal("wrap"), .trigger("rising"), .behavior("old")) counter_1 (
    .count(not_3_out), .Q(counter_1_q), .clk(CLK), .clr(RST));  // open: load, D, carry, preset
  // Probe on Yn_1_2_q[1]
  Register #(.width(1), .trigger("rising"), .Select("low")) Yn_1_2 (
    .D(P_star[0]), .en(not_3_out), .Q(Yn_1_2_q[1]), .clk(CLK), .clr(RST));
  Comparator #(.width(4), .mode("unsigned")) comparator_1 (
    .a(counter_1_q), .b(4'b1001), .eq(comparator_1_eq));  // open: gt, lt
  D_Flip_Flop #(.trigger("rising"), .Pre_Clr_Positions("LEGACY"), .NegatePresetClear("false"), .enable("true"), .NewFFLayout("false")) d_ff_1 (
    .clk(CLK), .D(1'b1), .Q(d_ff_1_q), .reset(RST));  // open: Qn, preset, en
  Button \u_时钟  (.out(CLK));
  not not_2 (END, not_3_out);
  not not_3 (not_3_out, comparator_1_eq);
  // Probe on \乘积 
  xor xor_1 (XYZ, XZ, YZ);
  Negator #(.width(16)) negator_1 (.in({PX[15], X, {7{1'b0}}}), .out({negator_1_out[15], PX_star}));
  Comparator #(.width(8), .mode("twosComplement")) comparator_2 (.a(X), .b(8'h80), .eq(PS[0]));  // open: gt, lt
  Comparator #(.width(8), .mode("twosComplement")) comparator_3 (.a(Y), .b(8'h80), .eq(PS[1]));  // open: gt, lt
  or or_1 (XZ, X[0], X[1], X[2], X[3], X[4], X[5], X[6], X[7]);
  LED #(.active("true")) led_1 (.in(END));
  xor xor_2 (PX[15], X[7], Y[7]);
  Negator #(.width(16)) negator_2 (.in({PX[15], Y, {7{1'b0}}}), .out({negator_2_out[15], PY_star}));
  Multiplexer #(.select(2), .width(16), .disabled("Z"), .enable("false")) multiplexer_3 (
    .in0(P_star), .in1({PX[15], PY_star}), .in2({PX[15], PX_star}), .in3(16'h4000), .out(multiplexer_3_out),
    .sel(PS));
  // Probe on X
  // Probe on Y
  // Probe on \乘积 
  or or_2 (YZ, Y[0], Y[1], Y[2], Y[3], Y[4], Y[5], Y[6], Y[7]);
  Multiplexer #(.select(1), .width(16), .disabled("Z"), .enable("false")) multiplexer_4 (
    .in0(multiplexer_3_out), .in1({16{1'b0}}), .out(\乘积 ), .sel(XYZ));

  // Other names for the same wires on the sheet: P[15:0] = \乘积 ; PX[14:7] = X; SX = X[7]; PY[15:7] = {PX[15], Y};
  //   SY = Y[7]; PX_star[15] = PX[15]; PY_star[15] = PX[15]; SP = PX[15]

  // Notes on the sheet:
  //   输入引脚区
  //   功能说明: 8位补码一位乘法器                输入：X、Y 为8位补码               输出：乘积=X*Y 为16位补码
  //   首先设置X、Y值，然后按“复位”按钮，接下去按“CLK”按钮多次，直到“END”指示灯变红，此时观看乘积是不是正确？
  //   8位补码一位乘法器（复杂版）
  //   输出引脚区
  //   ×
  //   =
endmodule

module \_8位补码一位乘法器_用8位无符号数一位乘法器实现  (
  input  [7:0] X,
  input  [7:0] Y,
  output [15:0] \乘积 
);

  wire CLK, END, RST;

  // Probe on X
  // Probe on Y
  Button \u_复位  (.out(RST));
  Button \u_时钟  (.out(CLK));
  // Probe on \乘积 
  LED #(.active("true")) led_1 (.in(END));
  // Probe on X
  // Probe on Y
  // Probe on \乘积 

  // Notes on the sheet:
  //   输入引脚区
  //   首先设置X、Y值，然后按“复位”按钮，接下去按“CLK”按钮多次，直到“END”指示灯变红，此时观看乘积是不是正确？
  //   功能说明: 8位补码一位乘法器（用8位无符号数一位乘法器实现）                输入：X、Y 为8位补码               输出：乘积=X*Y 为16位补码
  //   请同学们在此处设计电路！
  //   8位补码一位乘法器（用8位无符号数一位乘法器实现）
  //   输出引脚区
  //   ×
  //   =
endmodule

module \_8位串行加法器  (
  input  [7:0] X,
  input  [7:0] Y,
  input  Cin,
  output [7:0] S,
  output Cout,
  output out_6
);

  wire \n1位全加器_fa_2_cout , \n1位全加器_fa_3_cout , \n1位全加器_fa_4_cout , \n1位全加器_fa_5_cout , \n1位全加器_fa_6_cout ,
       \n1位全加器_fa_7_cout , \n1位全加器_fa_8_cout ;

  xor xor_1 (out_6, Cout, \n1位全加器_fa_2_cout );
  \_1位全加器_FA  \u_1位全加器_fa_1  (.Cout(Cout), .Si(S[7]), .Cin(\n1位全加器_fa_2_cout ), .Xi(X[7]), .Yi(Y[7]));
  \_1位全加器_FA  \u_1位全加器_fa_2  (.Cout(\n1位全加器_fa_2_cout ), .Si(S[6]), .Cin(\n1位全加器_fa_3_cout ), .Xi(X[6]), .Yi(Y[6]));
  \_1位全加器_FA  \u_1位全加器_fa_3  (.Cout(\n1位全加器_fa_3_cout ), .Si(S[5]), .Cin(\n1位全加器_fa_4_cout ), .Xi(X[5]), .Yi(Y[5]));
  \_1位全加器_FA  \u_1位全加器_fa_4  (.Cout(\n1位全加器_fa_4_cout ), .Si(S[4]), .Cin(\n1位全加器_fa_5_cout ), .Xi(X[4]), .Yi(Y[4]));
  \_1位全加器_FA  \u_1位全加器_fa_5  (.Cout(\n1位全加器_fa_5_cout ), .Si(S[3]), .Cin(\n1位全加器_fa_6_cout ), .Xi(X[3]), .Yi(Y[3]));
  \_1位全加器_FA  \u_1位全加器_fa_6  (.Cout(\n1位全加器_fa_6_cout ), .Si(S[2]), .Cin(\n1位全加器_fa_7_cout ), .Xi(X[2]), .Yi(Y[2]));
  // Probe on X
  // Probe on Y
  // Probe on S
  \_1位全加器_FA  \u_1位全加器_fa_7  (.Cout(\n1位全加器_fa_7_cout ), .Si(S[1]), .Cin(\n1位全加器_fa_8_cout ), .Xi(X[1]), .Yi(Y[1]));
  // Probe on X
  // Probe on Y
  // Probe on S
  \_1位全加器_FA  \u_1位全加器_fa_8  (.Cout(\n1位全加器_fa_8_cout ), .Si(S[0]), .Cin(Cin), .Xi(X[0]), .Yi(Y[0]));

  // Other names for the same wires on the sheet: OF = out_6

  // Notes on the sheet:
  //   Y: pull=down
  //   X: pull=down
  //   Cin: pull=down
  //   输入引脚区
  //   符号位
  //   输出引脚区
  //   8位串行加法器
  //   OF
  //   +
  //   有符号加法
  //   +
  //   =
  //   无符号加法
endmodule

// FA
module \_1位全加器_FA  (
  input  Cin,
  input  Xi,
  input  Yi,
  output Cout,
  output Si
);

  wire AND_2_out, AND_out, XOR_2_out;

  and AND (AND_out, Xi, Yi);
  or OR (Cout, AND_out, AND_2_out);
  and AND_2 (AND_2_out, Cin, XOR_2_out);
  xor XOR (Si, Cin, XOR_2_out);
  xor XOR_2 (XOR_2_out, Xi, Yi);

  // Notes on the sheet:
  //   Cin: pull=down
  //   Yi: pull=down
  //   Xi: pull=down
  //   Cout = Xi Yi + Cin (Xi ^ Yi)
  //   Si = Xi ^ Yi ^ Cin
  //   1位全加器（FA）
endmodule

module \备用  (
  input  [7:0] X,
  input  [7:0] Y,
  output [15:0] \乘积 
);

  wire CLK, comparator_1_eq, d_ff_1_q, END, not_1_out, RST;
  wire [0:0] \n8位串行加法器_1_s ;
  wire [3:0] counter_1_q;
  wire [7:0] multiplexer_1_out, multiplexer_2_out, \n8位串行加法器_1_cout ;

  Button \u_复位  (.out(RST));
  // Probe on \乘积 [15:8]
  Register #(.width(8), .trigger("rising"), .Select("low")) register_1 (
    .D(\n8位串行加法器_1_cout ), .en(not_1_out), .Q(\乘积 [15:8]), .clk(CLK), .clr(RST));
  \_8位串行加法器  \u_8位串行加法器_1  (
    .X(\乘积 [15:8]), .Y(multiplexer_1_out), .Cin(1'b0), .S({\n8位串行加法器_1_cout [6:0], \n8位串行加法器_1_s [0]}),
    .Cout(\n8位串行加法器_1_cout [7]));  // open: out_6
  Multiplexer #(.select(1), .width(8), .disabled("Z"), .enable("false")) multiplexer_1 (
    .in0({8{1'b0}}), .in1(X), .out(multiplexer_1_out), .sel(\乘积 [0]));
  Button u_CLK (.out(CLK));
  Multiplexer #(.select(1), .width(8), .disabled("Z"), .enable("false")) multiplexer_2 (
    .in0(Y), .in1({\n8位串行加法器_1_s [0], \乘积 [7:1]}), .out(multiplexer_2_out), .sel(d_ff_1_q));
  // Probe on \乘积 [7:0]
  Register #(.width(8), .trigger("rising"), .Select("low")) Y_2 (
    .D(multiplexer_2_out), .en(not_1_out), .Q(\乘积 [7:0]), .clk(CLK), .clr(RST));
  Counter #(.width(4), .max('hf), .ongoal("wrap"), .trigger("rising"), .behavior("old")) counter_1 (
    .count(not_1_out), .Q(counter_1_q), .clk(CLK), .clr(RST));  // open: load, D, carry, preset
  D_Flip_Flop #(.trigger("rising"), .Pre_Clr_Positions("LEGACY"), .NegatePresetClear("false"), .enable("true"), .NewFFLayout("false")) d_ff_1 (
    .clk(CLK), .D(1'b1), .Q(d_ff_1_q), .reset(RST));  // open: Qn, preset, en
  not not_1 (not_1_out, comparator_1_eq);
  Comparator #(.width(4), .mode("unsigned")) comparator_1 (
    .a(counter_1_q), .b(4'b1001), .eq(comparator_1_eq));  // open: gt, lt
  LED #(.active("true")) led_1 (.in(END));
  not not_2 (END, not_1_out);
  // Probe on X
  // Probe on Y
  // Probe on \乘积 

  // Notes on the sheet:
  //   输入引脚区
  //   ∑
  //   功能说明: 8位无符号数一位乘法器                输入：X、Y 为8位无符号数               输出：乘积=X*Y 为16位无符号数
  //   首先设置X、Y值，然后按“复位”按钮，接下去按“CLK”按钮多次，直到“END”指示灯变红，此时观看乘积是不是正确？
  //   8位无符号数一位乘法器
  //   输出引脚区
  //   ×
  //   =
endmodule
