// Logisim project 阵列乘法器.circ as structural Verilog: 6 circuits, main circuit 5位无符号阵列乘法器（横向）
// 5位阵列乘法器（斜向）
module \_5位无符号阵列乘法器_斜向  (
  input  [4:0] X,
  input  [4:0] Y,
  output [9:0] \乘积 
);

  wire \n1位全加器fa_2_cout , \n1位全加器fa_2_si , \n1位全加器fa_3_cout , \n1位全加器fa_4_cout , \n1位全加器fa_4_si ,
       \n1位全加器fa_5_cout , \n1位全加器fa_5_si , \n1位全加器fa_6_cout , \n1位全加器fa_7_cout , \n1位全加器fa_7_si ,
       \n1位全加器fa_8_cout , \n1位全加器fa_8_si , \n1位全加器fa_9_cout , \n1位全加器fa_9_si , \n1位全加器fa_10_cout ,
       \n1位全加器fa_11_cout , \n1位全加器fa_11_si , \n1位全加器fa_12_cout , \n1位全加器fa_12_si , \n1位全加器fa_13_cout ,
       \n1位全加器fa_13_si , \n1位全加器fa_14_cout , \n1位全加器fa_15_cout , \n1位全加器fa_15_si , \n1位全加器fa_16_cout ,
       \n1位全加器fa_16_si , \n1位全加器fa_17_cout , \n1位全加器fa_18_cout , \n1位全加器fa_18_si , \n1位全加器fa_19_cout ,
       \n1位全加器fa_20_cout , X0Y1, X0Y2, X0Y3, X0Y4, X1Y0, X1Y1, X1Y2, X1Y3, X1Y4, X2Y0, X2Y1, X2Y2, X2Y3,
       X2Y4, X3Y0, X3Y1, X3Y2, X3Y3, X3Y4, X4Y0, X4Y1, X4Y2, X4Y3, X4Y4;

  \_1位全加器FA  \u_1位全加器fa_1  (.Cout(\乘积 [9]), .Si(\乘积 [8]), .Cin(\n1位全加器fa_2_cout ), .Xi(\n1位全加器fa_3_cout ), .Yi(X4Y4));
  \与门阵列  \u_与门阵列_1  (
    .X(X), .XY4({X4Y4, X3Y4, X2Y4, X1Y4, X0Y4}), .XY3({X4Y3, X3Y3, X2Y3, X1Y3, X0Y3}),
    .XY2({X4Y2, X3Y2, X2Y2, X1Y2, X0Y2}), .XY1({X4Y1, X3Y1, X2Y1, X1Y1, X0Y1}),
    .XY0({X4Y0, X3Y0, X2Y0, X1Y0, \乘积 [0]}), .Y(Y));
  \_1位全加器FA  \u_1位全加器fa_2  (
    .Cout(\n1位全加器fa_2_cout ), .Si(\n1位全加器fa_2_si ), .Cin(\n1位全加器fa_4_cout ), .Xi(X3Y4), .Yi(X4Y3));
  \_1位全加器FA  \u_1位全加器fa_3  (
    .Cout(\n1位全加器fa_3_cout ), .Si(\乘积 [7]), .Cin(\n1位全加器fa_5_cout ), .Xi(\n1位全加器fa_6_cout ),
    .Yi(\n1位全加器fa_2_si ));
  \_1位全加器FA  \u_1位全加器fa_4  (
    .Cout(\n1位全加器fa_4_cout ), .Si(\n1位全加器fa_4_si ), .Cin(\n1位全加器fa_7_cout ), .Xi(X3Y3), .Yi(X4Y2));
  \_1位全加器FA  \u_1位全加器fa_5  (
    .Cout(\n1位全加器fa_5_cout ), .Si(\n1位全加器fa_5_si ), .Cin(\n1位全加器fa_8_cout ), .Xi(X2Y4), .Yi(\n1位全加器fa_4_si ));
  \_1位全加器FA  \u_1位全加器fa_6  (
    .Cout(\n1位全加器fa_6_cout ), .Si(\乘积 [6]), .Cin(\n1位全加器fa_9_cout ), .Xi(\n1位全加器fa_10_cout ),
    .Yi(\n1位全加器fa_5_si ));
  \_1位全加器FA  \u_1位全加器fa_7  (
    .Cout(\n1位全加器fa_7_cout ), .Si(\n1位全加器fa_7_si ), .Cin(\n1位全加器fa_11_cout ), .Xi(X3Y2), .Yi(X4Y1));
  \_1位全加器FA  \u_1位全加器fa_8  (
    .Cout(\n1位全加器fa_8_cout ), .Si(\n1位全加器fa_8_si ), .Cin(\n1位全加器fa_12_cout ), .Xi(X2Y3), .Yi(\n1位全加器fa_7_si ));
  \_1位全加器FA  \u_1位全加器fa_9  (
    .Cout(\n1位全加器fa_9_cout ), .Si(\n1位全加器fa_9_si ), .Cin(\n1位全加器fa_13_cout ), .Xi(X1Y4), .Yi(\n1位全加器fa_8_si ));
  \_1位全加器FA  \u_1位全加器fa_10  (
    .Cout(\n1位全加器fa_10_cout ), .Si(\乘积 [5]), .Cin(\n1位全加器fa_14_cout ), .Xi(1'b0), .Yi(\n1位全加器fa_9_si ));
  \_1位全加器FA  \u_1位全加器fa_11  (.Cout(\n1位全加器fa_11_cout ), .Si(\n1位全加器fa_11_si ), .Cin(1'b0), .Xi(X3Y1), .Yi(X4Y0));
  \_1位全加器FA  \u_1位全加器fa_12  (
    .Cout(\n1位全加器fa_12_cout ), .Si(\n1位全加器fa_12_si ), .Cin(\n1位全加器fa_15_cout ), .Xi(X2Y2),
    .Yi(\n1位全加器fa_11_si ));
  \_1位全加器FA  \u_1位全加器fa_13  (
    .Cout(\n1位全加器fa_13_cout ), .Si(\n1位全加器fa_13_si ), .Cin(\n1位全加器fa_16_cout ), .Xi(X1Y3),
    .Yi(\n1位全加器fa_12_si ));
  \_1位全加器FA  \u_1位全加器fa_14  (
    .Cout(\n1位全加器fa_14_cout ), .Si(\乘积 [4]), .Cin(\n1位全加器fa_17_cout ), .Xi(X0Y4), .Yi(\n1位全加器fa_13_si ));
  \_1位全加器FA  \u_1位全加器fa_15  (.Cout(\n1位全加器fa_15_cout ), .Si(\n1位全加器fa_15_si ), .Cin(1'b0), .Xi(X2Y1), .Yi(X3Y0));
  \_1位全加器FA  \u_1位全加器fa_16  (
    .Cout(\n1位全加器fa_16_cout ), .Si(\n1位全加器fa_16_si ), .Cin(\n1位全加器fa_18_cout ), .Xi(X1Y2),
    .Yi(\n1位全加器fa_15_si ));
  \_1位全加器FA  \u_1位全加器fa_17  (
    .Cout(\n1位全加器fa_17_cout ), .Si(\乘积 [3]), .Cin(\n1位全加器fa_19_cout ), .Xi(X0Y3), .Yi(\n1位全加器fa_16_si ));
  \_1位全加器FA  \u_1位全加器fa_18  (.Cout(\n1位全加器fa_18_cout ), .Si(\n1位全加器fa_18_si ), .Cin(1'b0), .Xi(X1Y1), .Yi(X2Y0));
  \_1位全加器FA  \u_1位全加器fa_19  (
    .Cout(\n1位全加器fa_19_cout ), .Si(\乘积 [2]), .Cin(\n1位全加器fa_20_cout ), .Xi(X0Y2), .Yi(\n1位全加器fa_18_si ));
  \_1位全加器FA  \u_1位全加器fa_20  (.Cout(\n1位全加器fa_20_cout ), .Si(\乘积 [1]), .Cin(1'b0), .Xi(X0Y1), .Yi(X1Y0));
  // Probe on X
  // Probe on Y
  // Probe on \乘积 

  // Other names for the same wires on the sheet: P[9:0] = \乘积 ; P0 = \乘积 [0]; X0Y0 = \乘积 [0];
  //   XY0[4:0] = {X4Y0, X3Y0, X2Y0, X1Y0, \乘积 [0]}; P1 = \乘积 [1]; P2 = \乘积 [2]; P3 = \乘积 [3]; P4 = \乘积 [4];
  //   P5 = \乘积 [5]; P6 = \乘积 [6]; P7 = \乘积 [7]; P8 = \乘积 [8]; P9 = \乘积 [9]; XY1[4:0] = {X4Y1, X3Y1, X2Y1, X1Y1, X0Y1};
  //   XY2[4:0] = {X4Y2, X3Y2, X2Y2, X1Y2, X0Y2}; XY3[4:0] = {X4Y3, X3Y3, X2Y3, X1Y3, X0Y3};
  //   XY4[4:0] = {X4Y4, X3Y4, X2Y4, X1Y4, X0Y4}

  // Notes on the sheet:
  //   Y: pull=down
  //   X: pull=down
  //   输入引脚区
  //   5位无符号阵列乘法器（斜向）
  //   输出引脚区
  //   ×
  //   =
  //   验证
endmodule

// 5位阵列乘法器（横向）
module \_5位无符号阵列乘法器_横向  (
  input  [4:0] X,
  input  [4:0] Y,
  output [9:0] \乘积 
);

  wire \n1位全加器fa_2_cout , \n1位全加器fa_2_si , \n1位全加器fa_3_cout , \n1位全加器fa_4_cout , \n1位全加器fa_4_si ,
       \n1位全加器fa_5_cout , \n1位全加器fa_5_si , \n1位全加器fa_6_cout , \n1位全加器fa_7_cout , \n1位全加器fa_7_si ,
       \n1位全加器fa_8_cout , \n1位全加器fa_8_si , \n1位全加器fa_9_cout , \n1位全加器fa_9_si , \n1位全加器fa_10_cout ,
       \n1位全加器fa_11_cout , \n1位全加器fa_11_si , \n1位全加器fa_12_cout , \n1位全加器fa_12_si , \n1位全加器fa_13_cout ,
       \n1位全加器fa_13_si , \n1位全加器fa_14_cout , \n1位全加器fa_15_cout , \n1位全加器fa_15_si , \n1位全加器fa_16_cout ,
       \n1位全加器fa_16_si , \n1位全加器fa_17_cout , \n1位全加器fa_18_cout , \n1位全加器fa_18_si , \n1位全加器fa_19_cout ,
       \n1位全加器fa_20_cout , X0Y1, X0Y2, X0Y3, X0Y4, X1Y0, X1Y1, X1Y2, X1Y3, X1Y4, X2Y0, X2Y1, X2Y2, X2Y3,
       X2Y4, X3Y0, X3Y1, X3Y2, X3Y3, X3Y4, X4Y0, X4Y1, X4Y2, X4Y3, X4Y4;

  \_1位全加器FA  \u_1位全加器fa_1  (.Cout(\乘积 [9]), .Si(\乘积 [8]), .Cin(X4Y4), .Xi(\n1位全加器fa_3_cout ), .Yi(\n1位全加器fa_2_cout ));
  \与门阵列  \u_与门阵列_1  (
    .X(X), .XY4({X4Y4, X3Y4, X2Y4, X1Y4, X0Y4}), .XY3({X4Y3, X3Y3, X2Y3, X1Y3, X0Y3}),
    .XY2({X4Y2, X3Y2, X2Y2, X1Y2, X0Y2}), .XY1({X4Y1, X3Y1, X2Y1, X1Y1, X0Y1}),
    .XY0({X4Y0, X3Y0, X2Y0, X1Y0, \乘积 [0]}), .Y(Y));
  \_1位全加器FA  \u_1位全加器fa_2  (
    .Cout(\n1位全加器fa_2_cout ), .Si(\n1位全加器fa_2_si ), .Cin(X4Y3), .Xi(\n1位全加器fa_5_cout ), .Yi(\n1位全加器fa_4_cout ));
  \_1位全加器FA  \u_1位全加器fa_3  (
    .Cout(\n1位全加器fa_3_cout ), .Si(\乘积 [7]), .Cin(X3Y4), .Xi(\n1位全加器fa_6_cout ), .Yi(\n1位全加器fa_2_si ));
  \_1位全加器FA  \u_1位全加器fa_4  (
    .Cout(\n1位全加器fa_4_cout ), .Si(\n1位全加器fa_4_si ), .Cin(X4Y2), .Xi(\n1位全加器fa_8_cout ), .Yi(\n1位全加器fa_7_cout ));
  \_1位全加器FA  \u_1位全加器fa_5  (
    .Cout(\n1位全加器fa_5_cout ), .Si(\n1位全加器fa_5_si ), .Cin(X3Y3), .Xi(\n1位全加器fa_9_cout ), .Yi(\n1位全加器fa_4_si ));
  \_1位全加器FA  \u_1位全加器fa_6  (
    .Cout(\n1位全加器fa_6_cout ), .Si(\乘积 [6]), .Cin(X2Y4), .Xi(\n1位全加器fa_10_cout ), .Yi(\n1位全加器fa_5_si ));
  \_1位全加器FA  \u_1位全加器fa_7  (
    .Cout(\n1位全加器fa_7_cout ), .Si(\n1位全加器fa_7_si ), .Cin(X4Y1), .Xi(\n1位全加器fa_11_cout ), .Yi(1'b0));
  \_1位全加器FA  \u_1位全加器fa_8  (
    .Cout(\n1位全加器fa_8_cout ), .Si(\n1位全加器fa_8_si ), .Cin(X3Y2), .Xi(\n1位全加器fa_12_cout ), .Yi(\n1位全加器fa_7_si ));
  \_1位全加器FA  \u_1位全加器fa_9  (
    .Cout(\n1位全加器fa_9_cout ), .Si(\n1位全加器fa_9_si ), .Cin(X2Y3), .Xi(\n1位全加器fa_13_cout ), .Yi(\n1位全加器fa_8_si ));
  \_1位全加器FA  \u_1位全加器fa_10  (
    .Cout(\n1位全加器fa_10_cout ), .Si(\乘积 [5]), .Cin(X1Y4), .Xi(\n1位全加器fa_14_cout ), .Yi(\n1位全加器fa_9_si ));
  \_1位全加器FA  \u_1位全加器fa_11  (
    .Cout(\n1位全加器fa_11_cout ), .Si(\n1位全加器fa_11_si ), .Cin(X3Y1), .Xi(\n1位全加器fa_15_cout ), .Yi(X4Y0));
  \_1位全加器FA  \u_1位全加器fa_12  (
    .Cout(\n1位全加器fa_12_cout ), .Si(\n1位全加器fa_12_si ), .Cin(X2Y2), .Xi(\n1位全加器fa_16_cout ),
    .Yi(\n1位全加器fa_11_si ));
  \_1位全加器FA  \u_1位全加器fa_13  (
    .Cout(\n1位全加器fa_13_cout ), .Si(\n1位全加器fa_13_si ), .Cin(X1Y3), .Xi(\n1位全加器fa_17_cout ),
    .Yi(\n1位全加器fa_12_si ));
  \_1位全加器FA  \u_1位全加器fa_14  (.Cout(\n1位全加器fa_14_cout ), .Si(\乘积 [4]), .Cin(X0Y4), .Xi(1'b0), .Yi(\n1位全加器fa_13_si ));
  \_1位全加器FA  \u_1位全加器fa_15  (
    .Cout(\n1位全加器fa_15_cout ), .Si(\n1位全加器fa_15_si ), .Cin(X2Y1), .Xi(\n1位全加器fa_18_cout ), .Yi(X3Y0));
  \_1位全加器FA  \u_1位全加器fa_16  (
    .Cout(\n1位全加器fa_16_cout ), .Si(\n1位全加器fa_16_si ), .Cin(X1Y2), .Xi(\n1位全加器fa_19_cout ),
    .Yi(\n1位全加器fa_15_si ));
  \_1位全加器FA  \u_1位全加器fa_17  (.Cout(\n1位全加器fa_17_cout ), .Si(\乘积 [3]), .Cin(X0Y3), .Xi(1'b0), .Yi(\n1位全加器fa_16_si ));
  \_1位全加器FA  \u_1位全加器fa_18  (
    .Cout(\n1位全加器fa_18_cout ), .Si(\n1位全加器fa_18_si ), .Cin(X1Y1), .Xi(\n1位全加器fa_20_cout ), .Yi(X2Y0));
  \_1位全加器FA  \u_1位全加器fa_19  (.Cout(\n1位全加器fa_19_cout ), .Si(\乘积 [2]), .Cin(X0Y2), .Xi(1'b0), .Yi(\n1位全加器fa_18_si ));
  \_1位全加器FA  \u_1位全加器fa_20  (.Cout(\n1位全加器fa_20_cout ), .Si(\乘积 [1]), .Cin(X0Y1), .Xi(1'b0), .Yi(X1Y0));
  // Probe on X
  // Probe on Y
  // Probe on \乘积 

  // Other names for the same wires on the sheet: P[9:0] = \乘积 ; P0 = \乘积 [0]; X0Y0 = \乘积 [0];
  //   XY0[4:0] = {X4Y0, X3Y0, X2Y0, X1Y0, \乘积 [0]}; P1 = \乘积 [1]; P2 = \乘积 [2]; P3 = \乘积 [3]; P4 = \乘积 [4];
  //   P5 = \乘积 [5]; P6 = \乘积 [6]; P7 = \乘积 [7]; P8 = \乘积 [8]; P9 = \乘积 [9]; XY1[4:0] = {X4Y1, X3Y1, X2Y1, X1Y1, X0Y1};
  //   XY2[4:0] = {X4Y2, X3Y2, X2Y2, X1Y2, X0Y2}; XY3[4:0] = {X4Y3, X3Y3, X2Y3, X1Y3, X0Y3};
  //   XY4[4:0] = {X4Y4, X3Y4, X2Y4, X1Y4, X0Y4}

  // Notes on the sheet:
  //   Y: pull=down
  //   X: pull=down
  //   输入引脚区
  //   5位无符号阵列乘法器（横向）
  //   输出引脚区
  //   ×
  //   =
  //   验证
endmodule

module \_6位原码阵列乘法器  (
  input  [5:0] X,
  input  [5:0] Y,
  output [10:0] P
);

  wire comparator_1_eq, comparator_2_eq, comparator_3_eq;
  wire [5:0] adder_1_out, adder_3_out, multiplexer_1_out, multiplexer_3_out, not_1_out, not_3_out, \X真值 ,
       \Y真值 ;
  wire [10:0] adder_2_out, multiplexer_2_out, not_2_out, \P真值 ;

  // Probe on X[4:0]
  // Probe on Y[4:0]
  \_5位无符号阵列乘法器_斜向  \u_5位无符号阵列乘法器_斜向_1  (.\乘积 (P[9:0]), .X(Y[4:0]), .Y(X[4:0]));
  // Probe on P[9:0]
  xor xor_1 (P[10], X[5], Y[5]);
  assign not_1_out = ~X;  // NOT_Gate not_1, 6 bits wide
  Adder #(.width(6)) adder_1 (.a(not_1_out), .b(6'b000001), .out(adder_1_out));  // open: cin, cout
  assign not_2_out = ~P;  // NOT_Gate not_2, 11 bits wide
  Adder #(.width(11)) adder_2 (.a(not_2_out), .b(11'h1), .out(adder_2_out));  // open: cin, cout
  assign not_3_out = ~Y;  // NOT_Gate not_3, 6 bits wide
  Adder #(.width(6)) adder_3 (.a(not_3_out), .b(6'b000001), .out(adder_3_out));  // open: cin, cout
  Multiplexer #(.select(1), .width(6), .disabled("Z"), .enable("false")) multiplexer_1 (
    .in0(X), .in1(adder_1_out), .out(multiplexer_1_out), .sel(X[5]));
  Multiplexer #(.select(1), .width(11), .disabled("Z"), .enable("false")) multiplexer_2 (
    .in0(P), .in1(adder_2_out), .out(multiplexer_2_out), .sel(P[10]));
  Multiplexer #(.select(1), .width(6), .disabled("Z"), .enable("false")) multiplexer_3 (
    .in0(Y), .in1(adder_3_out), .out(multiplexer_3_out), .sel(Y[5]));
  // Probe on \X真值 
  // Probe on \Y真值 
  // Probe on \P真值 
  Comparator #(.width(5), .mode("twosComplement")) comparator_1 (
    .a(multiplexer_1_out[4:0]), .b({5{1'b0}}), .eq(comparator_1_eq));  // open: gt, lt
  Comparator #(.width(10), .mode("twosComplement")) comparator_2 (
    .a(multiplexer_2_out[9:0]), .b({10{1'b0}}), .eq(comparator_2_eq));  // open: gt, lt
  Comparator #(.width(5), .mode("twosComplement")) comparator_3 (
    .a(multiplexer_3_out[4:0]), .b({5{1'b0}}), .eq(comparator_3_eq));  // open: gt, lt
  Multiplexer #(.select(1), .width(6), .disabled("Z"), .enable("false")) multiplexer_4 (
    .in0({X[5], multiplexer_1_out[4:0]}), .in1({6{1'b0}}), .out(\X真值 ), .sel(comparator_1_eq));
  Multiplexer #(.select(1), .width(11), .disabled("Z"), .enable("false")) multiplexer_5 (
    .in0({P[10], multiplexer_2_out[9:0]}), .in1({11{1'b0}}), .out(\P真值 ), .sel(comparator_2_eq));
  Multiplexer #(.select(1), .width(6), .disabled("Z"), .enable("false")) multiplexer_6 (
    .in0({Y[5], multiplexer_3_out[4:0]}), .in1({6{1'b0}}), .out(\Y真值 ), .sel(comparator_3_eq));

  // Other names for the same wires on the sheet: Sx = X[5]; S = P[10]; Sy = Y[5]; P_t[9:0] = P[9:0];
  //   X_t[4:0] = X[4:0]; Y_t[4:0] = Y[4:0]

  // Notes on the sheet:
  //   输入引脚区
  //    功能说明：6位原码阵列乘法器          输入：X（6位原码）、Y（6位原码）          输出：P（11位原码）= X×Y
  //   6位原码阵列乘法器
  //   输出引脚区
  //   验证
  //   ×
  //   =
endmodule

module \_6位补码阵列乘法器  (
  input  [5:0] X,
  input  [5:0] Y,
  output [11:0] P
);

  wire and_1_out, comparator_1_eq, comparator_2_eq, comparator_3_eq, comparator_4_eq, comparator_5_eq,
       comparator_6_eq, comparator_7_eq, comparator_8_eq, comparator_9_eq, comparator_10_eq,
       comparator_11_eq, comparator_12_eq, comparator_13_eq, comparator_14_eq, comparator_15_eq,
       comparator_16_eq, comparator_17_eq, comparator_18_eq, not_4_out, not_5_out, or_1_out, or_2_out,
       or_3_out, or_4_out;
  wire [4:0] X_t, Y_t;
  wire [5:0] adder_1_out, adder_2_out, not_1_out, not_2_out;
  wire [5:5] multiplexer_1_out, multiplexer_2_out;
  wire [9:0] adder_3_out, adder_4_out, adder_5_out, multiplexer_8_out, multiplexer_9_out,
       \n5位无符号阵列乘法器_斜向_1_乘积 , \n5位无符号阵列乘法器_斜向_2_乘积 , \n5位无符号阵列乘法器_斜向_3_乘积 , negator_1_out, negator_2_out,
       not_3_out, P2, P3;
  wire [11:0] P1;

  assign not_1_out = ~X;  // NOT_Gate not_1, 6 bits wide
  assign not_2_out = ~Y;  // NOT_Gate not_2, 6 bits wide
  Comparator #(.width(6), .mode("twosComplement")) comparator_1 (
    .a(X), .b({6{1'b0}}), .eq(comparator_1_eq));  // open: gt, lt
  Comparator #(.width(6), .mode("twosComplement")) comparator_2 (
    .a(X), .b(6'b100000), .eq(comparator_2_eq));  // open: gt, lt
  Comparator #(.width(6), .mode("twosComplement")) comparator_3 (
    .a(Y), .b({6{1'b0}}), .eq(comparator_3_eq));  // open: gt, lt
  Comparator #(.width(6), .mode("twosComplement")) comparator_4 (
    .a(Y), .b(6'b100000), .eq(comparator_4_eq));  // open: gt, lt
  Multiplexer #(.select(1), .width(6), .disabled("Z"), .enable("false")) multiplexer_1 (
    .in0(X), .in1(adder_1_out), .out({multiplexer_1_out[5], X_t}), .sel(X[5]));
  Adder #(.width(6)) adder_1 (.a(not_1_out), .b(6'b000001), .out(adder_1_out));  // open: cin, cout
  Multiplexer #(.select(1), .width(6), .disabled("Z"), .enable("false")) multiplexer_2 (
    .in0(Y), .in1(adder_2_out), .out({multiplexer_2_out[5], Y_t}), .sel(Y[5]));
  Adder #(.width(6)) adder_2 (.a(not_2_out), .b(6'b000001), .out(adder_2_out));  // open: cin, cout
  or or_1 (or_1_out, comparator_1_eq, comparator_2_eq, comparator_3_eq, comparator_4_eq);
  Multiplexer #(.select(1), .width(12), .disabled("Z"), .enable("false")) multiplexer_3 (
    .in0({{2{P1[11]}}, P1[9:0]}), .out(P), .sel(or_1_out));  // open: in1
  assign not_3_out = ~\n5位无符号阵列乘法器_斜向_1_乘积 ;  // NOT_Gate not_3, 10 bits wide
  \_5位无符号阵列乘法器_斜向  \u_5位无符号阵列乘法器_斜向_1  (.\乘积 (\n5位无符号阵列乘法器_斜向_1_乘积 ), .X(Y_t), .Y(X_t));
  Comparator #(.width(6), .mode("twosComplement")) comparator_5 (
    .a(X), .b({6{1'b0}}), .eq(comparator_5_eq));  // open: gt, lt
  not not_4 (not_4_out, comparator_6_eq);
  Comparator #(.width(6), .mode("twosComplement")) comparator_6 (
    .a(X), .b(6'b100000), .eq(comparator_6_eq));  // open: gt, lt
  Comparator #(.width(6), .mode("twosComplement")) comparator_7 (
    .a(Y), .b({6{1'b0}}), .eq(comparator_7_eq));  // open: gt, lt
  Comparator #(.width(6), .mode("twosComplement")) comparator_8 (
    .a(Y), .b(6'b100000), .eq(comparator_8_eq));  // open: gt, lt
  Adder #(.width(10)) adder_3 (.a(not_3_out), .b(10'h1), .out(adder_3_out));  // open: cin, cout
  Multiplexer #(.select(1), .width(12), .disabled("Z"), .enable("false")) multiplexer_4 (
    .in0({{2{P1[11]}}, P2}), .out(P), .sel(or_2_out));  // open: in1
  or or_2 (or_2_out, comparator_5_eq, not_4_out, comparator_7_eq, comparator_8_eq);
  Multiplexer #(.select(1), .width(10), .disabled("Z"), .enable("false")) multiplexer_5 (
    .in0(\n5位无符号阵列乘法器_斜向_1_乘积 ), .in1(adder_3_out), .out(P1[9:0]), .sel(P1[11]));
  // Probe on X
  // Probe on Y
  // Probe on P
  xor xor_1 (P1[11], X[5], Y[5]);
  Comparator #(.width(6), .mode("twosComplement")) comparator_9 (
    .a(X), .b({6{1'b0}}), .eq(comparator_9_eq));  // open: gt, lt
  Comparator #(.width(6), .mode("twosComplement")) comparator_10 (
    .a(X), .b(6'b100000), .eq(comparator_10_eq));  // open: gt, lt
  Comparator #(.width(6), .mode("twosComplement")) comparator_11 (
    .a(Y), .b({6{1'b0}}), .eq(comparator_11_eq));  // open: gt, lt
  Comparator #(.width(6), .mode("twosComplement")) comparator_12 (
    .a(Y), .b(6'b100000), .eq(comparator_12_eq));  // open: gt, lt
  not not_5 (not_5_out, comparator_12_eq);
  Multiplexer #(.select(1), .width(12), .disabled("Z"), .enable("false")) multiplexer_6 (
    .in0({{2{P1[11]}}, P3}), .out(P), .sel(or_3_out));  // open: in1
  or or_3 (or_3_out, comparator_9_eq, comparator_10_eq, comparator_11_eq, not_5_out);
  \_5位无符号阵列乘法器_斜向  \u_5位无符号阵列乘法器_斜向_2  (.\乘积 (\n5位无符号阵列乘法器_斜向_2_乘积 ), .X({5{1'b1}}), .Y(Y_t));
  \_5位无符号阵列乘法器_斜向  \u_5位无符号阵列乘法器_斜向_3  (.\乘积 (\n5位无符号阵列乘法器_斜向_3_乘积 ), .X({5{1'b1}}), .Y(X_t));
  Comparator #(.width(6), .mode("twosComplement")) comparator_13 (
    .a(X), .b(6'b100000), .eq(comparator_13_eq));  // open: gt, lt
  Comparator #(.width(6), .mode("twosComplement")) comparator_14 (
    .a(Y), .b(6'b100000), .eq(comparator_14_eq));  // open: gt, lt
  // Probe on adder_4_out
  Adder #(.width(10)) adder_4 (.a(\n5位无符号阵列乘法器_斜向_2_乘积 ), .b({{5{1'b0}}, Y_t}), .out(adder_4_out));  // open: cin, cout
  Comparator #(.width(6), .mode("twosComplement")) comparator_15 (
    .a(X), .b(6'b100000), .eq(comparator_15_eq));  // open: gt, lt
  Adder #(.width(10)) adder_5 (.a(\n5位无符号阵列乘法器_斜向_3_乘积 ), .b({{5{1'b0}}, X_t}), .out(adder_5_out));  // open: cin, cout
  Comparator #(.width(6), .mode("twosComplement")) comparator_16 (
    .a(Y), .b(6'b100000), .eq(comparator_16_eq));  // open: gt, lt
  Multiplexer #(.select(1), .width(12), .disabled("Z"), .enable("false")) multiplexer_7 (
    .in1(12'h400), .out(P), .sel(and_1_out));  // open: in0
  and and_1 (and_1_out, comparator_13_eq, comparator_14_eq);
  Multiplexer #(.select(1), .width(10), .disabled("Z"), .enable("false")) multiplexer_8 (
    .in1(adder_4_out), .out(multiplexer_8_out), .sel(comparator_15_eq));  // open: in0
  // Probe on adder_5_out
  Multiplexer #(.select(1), .width(10), .disabled("Z"), .enable("false")) multiplexer_9 (
    .in1(adder_5_out), .out(multiplexer_9_out), .sel(comparator_16_eq));  // open: in0
  Negator #(.width(10)) negator_1 (.in(multiplexer_8_out), .out(negator_1_out));
  Negator #(.width(10)) negator_2 (.in(multiplexer_9_out), .out(negator_2_out));
  Comparator #(.width(6), .mode("twosComplement")) comparator_17 (
    .a(X), .b({6{1'b0}}), .eq(comparator_17_eq));  // open: gt, lt
  or or_4 (or_4_out, comparator_17_eq, comparator_18_eq);
  Comparator #(.width(6), .mode("twosComplement")) comparator_18 (
    .a(Y), .b({6{1'b0}}), .eq(comparator_18_eq));  // open: gt, lt
  Multiplexer #(.select(1), .width(10), .disabled("Z"), .enable("false")) multiplexer_10 (
    .in0(multiplexer_8_out), .in1(negator_1_out), .out(P2), .sel(P1[11]));
  Multiplexer #(.select(1), .width(10), .disabled("Z"), .enable("false")) multiplexer_11 (
    .in0(multiplexer_9_out), .in1(negator_2_out), .out(P3), .sel(P1[11]));
  Multiplexer #(.select(1), .width(12), .disabled("Z"), .enable("false")) multiplexer_12 (
    .in1({12{1'b0}}), .out(P), .sel(or_4_out));  // open: in0

  // Other names for the same wires on the sheet: P1[10] = P1[11]; P2[11:10] = {2{P1[11]}}; P3[11:10] = {2{P1[11]}};
  //   S = P1[11]; XL[4:0] = X[4:0]; Sx = X[5]; YL[4:0] = Y[4:0]; Sy = Y[5]

  // Notes on the sheet:
  //   输入引脚区
  //    功能说明：6位补码阵列乘法器          输入：X（6位补码）、Y（6位补码）          输出：P（12位补码）= X×Y
  //   X！=-32，Y！=-32，X！=0，Y！=0的一般情况
  //   输出引脚区
  //   验证
  //   ×
  //   =
  //   选择结构
  //   6位补码阵列乘法器
  //   X=-32的情况
  //   Y=-32的情况
endmodule

module \与门阵列  (
  input  [4:0] X,
  input  [4:0] Y,
  output [4:0] XY0,
  output [4:0] XY1,
  output [4:0] XY2,
  output [4:0] XY3,
  output [4:0] XY4
);

  and and_1 (XY0[4], X[4], Y[0]);
  and and_2 (XY1[4], X[4], Y[1]);
  and and_3 (XY2[4], X[4], Y[2]);
  and and_4 (XY3[4], X[4], Y[3]);
  and and_5 (XY4[4], X[4], Y[4]);
  and and_6 (XY0[2], X[2], Y[0]);
  and and_7 (XY0[3], X[3], Y[0]);
  and and_8 (XY1[2], X[2], Y[1]);
  and and_9 (XY1[3], X[3], Y[1]);
  and and_10 (XY2[2], X[2], Y[2]);
  and and_11 (XY2[3], X[3], Y[2]);
  and and_12 (XY3[3], X[3], Y[3]);
  and and_13 (XY3[2], X[2], Y[3]);
  and and_14 (XY4[2], X[2], Y[4]);
  and and_15 (XY4[3], X[3], Y[4]);
  and and_16 (XY0[1], X[1], Y[0]);
  and and_17 (XY1[1], X[1], Y[1]);
  and and_18 (XY2[1], X[1], Y[2]);
  and and_19 (XY3[1], X[1], Y[3]);
  and and_20 (XY4[1], X[1], Y[4]);
  and and_21 (XY0[0], X[0], Y[0]);
  and and_22 (XY1[0], X[0], Y[1]);
  and and_23 (XY2[0], X[0], Y[2]);
  and and_24 (XY3[0], X[0], Y[3]);
  and and_25 (XY4[0], X[0], Y[4]);

  // Other names for the same wires on the sheet: X0Y0 = XY0[0]; X1Y0 = XY0[1]; X2Y0 = XY0[2]; X3Y0 = XY0[3];
  //   X4Y0 = XY0[4]; X0Y1 = XY1[0]; X1Y1 = XY1[1]; X2Y1 = XY1[2]; X3Y1 = XY1[3]; X4Y1 = XY1[4]; X0Y2 = XY2[0];
  //   X1Y2 = XY2[1]; X2Y2 = XY2[2]; X3Y2 = XY2[3]; X4Y2 = XY2[4]; X0Y3 = XY3[0]; X1Y3 = XY3[1]; X2Y3 = XY3[2];
  //   X3Y3 = XY3[3]; X4Y3 = XY3[4]; X0Y4 = XY4[0]; X1Y4 = XY4[1]; X2Y4 = XY4[2]; X3Y4 = XY4[3]; X4Y4 = XY4[4]

  // Notes on the sheet:
  //   5位乘法与门阵列
endmodule

module \_1位全加器FA  (
  input  Cin,
  input  Xi,
  input  Yi,
  output Cout,
  output Si
);

  wire AND_2_out, AND_out, XOR_2_out;

  or OR (Cout, AND_out, AND_2_out);
  and AND (AND_out, Xi, Yi);
  and AND_2 (AND_2_out, Cin, XOR_2_out);
  xor XOR (Si, Cin, XOR_2_out);
  xor XOR_2 (XOR_2_out, Xi, Yi);

  // Notes on the sheet:
  //   Cout = Xi Yi + Cin (Xi ^ Yi)
  //   Si = Xi ^ Yi ^ Cin
  //   1位全加器（FA）
endmodule
