// Logisim project 寄存器文件设计实验.circ as structural Verilog: 2 circuits, main circuit 寄存器文件电路（4个寄存器）
module \寄存器文件电路_4个寄存器  (
  input  [1:0] in_1,
  input  [1:0] in_2,
  input  [31:0] in_3,
  input  [1:0] in_4,
  input  in_5,
  input  in_6,
  output [31:0] out_7,
  output [31:0] out_8
);


  // Other names for the same wires on the sheet: CLK = in_6; Din[31:0] = in_3; R1_num[1:0] = in_1; R2_num[1:0] = in_2;
  //   RD1[31:0] = out_7; RD2[31:0] = out_8; W_num[1:0] = in_4; WE = in_5

  // Notes on the sheet:
  //   输入引脚
  //   请同学们在此设计电路！
  //   寄存器文件电路（4个寄存器）
  //   输出引脚
endmodule

module \寄存器文件电路_4个寄存器_R0_0  (
  input  [1:0] in_1,
  input  [1:0] in_2,
  input  [31:0] in_3,
  input  [1:0] in_4,
  input  in_5,
  input  in_6,
  output [31:0] out_7,
  output [31:0] out_8
);


  // Other names for the same wires on the sheet: CLK = in_6; Din[31:0] = in_3; R1_num[1:0] = in_1; R2_num[1:0] = in_2;
  //   RD1[31:0] = out_7; RD2[31:0] = out_8; W_num[1:0] = in_4; WE = in_5

  // Notes on the sheet:
  //   输入引脚
  //   请同学们在此设计电路！
  //   寄存器文件电路（4个寄存器，R0=0）
  //   输出引脚
endmodule
