// Logisim project 单总线结构MIPS处理器（微程序控制器）（7条指令）.circ as structural Verilog: 9 circuits, main circuit 单总线结构MIPS处理器（微程序控制器）数据通路
module \单总线结构MIPS处理器_微程序控制器_数据通路  (
);

  wire Add, Add4, alu_1_equal, and_1_out, ARin, CLK, comparator_1_eq, comparator_2_eq, DREin, DREout, DRin,
       DRout, equal, IR26out, IR_A_out, IR_I_out, IRin, J, not_1_out, PCin, PCout, PSWin, READ, RegDst,
       RegTgt, Rin, Rout, RST, Slt, Write, Xin, Zout;
  wire [4:0] registerfile_1_p4, registerfile_1_p5, \微地址_状态 ;
  wire [11:0] \指令数 , \时钟周期数 ;
  wire [31:0] alu_1_result, AR_q, bit_extender_1_out, bit_extender_2_out, controlled_buffer_1_out,
       controlled_buffer_3_out, DR_q, IR, PC_q, ram_1_data, registerfile_1_p6, shifter_1_out, X_q, Z_q,
       \内部总线 ;

  Button u_RST (.out(RST));
  // Probe on IR
  // Probe on \指令数 
  Register #(.width(32), .trigger("rising"), .Select("low")) AR (.D(\内部总线 ), .en(ARin), .Q(AR_q), .clk(CLK), .clr(RST));
  Register #(.width(32), .trigger("rising"), .Select("low")) X (.D(\内部总线 ), .en(Xin), .Q(X_q), .clk(CLK), .clr(RST));
  Clock #(.highDuration(1), .lowDuration(1)) u_CLK (.out(CLK));
  // Probe on \微地址_状态 
  // Probe on \时钟周期数 
  RAM #(.addrWidth(10), .dataWidth(32), .bus("separate"), .Select("high")) ram_1 (
    .addr(AR_q[11:2]), .din(controlled_buffer_3_out), .data(ram_1_data), .str(Write), .clk(CLK), .ld(READ));  // open: sel, clr
  ALU alu_1 (.X(X_q), .Y(\内部总线 ), .Equal(alu_1_equal), .Result(alu_1_result), .ADD(Add), .ADD4(Add4), .J(J), .SLT(Slt));
  assign controlled_buffer_1_out = DRin ? \内部总线  : 32'bz;  // Controlled_Buffer controlled_buffer_1
  assign controlled_buffer_1_out = DREin ? ram_1_data : 32'bz;  // Controlled_Buffer controlled_buffer_2
  assign controlled_buffer_3_out = DREout ? DR_q : 32'bz;  // Controlled_Buffer controlled_buffer_3
  Register #(.width(32), .trigger("rising"), .Select("low")) PC (.D(\内部总线 ), .en(PCin), .Q(PC_q), .clk(CLK), .clr(RST));
  Register #(.width(32), .trigger("rising"), .Select("low")) DR (
    .D(controlled_buffer_1_out), .Q(DR_q), .clk(CLK), .clr(RST));  // open: en
  Register #(.width(1), .trigger("rising"), .Select("low")) PSW (
    .D(alu_1_equal), .en(PSWin), .Q(equal), .clk(CLK), .clr(RST));
  Register #(.width(32), .trigger("rising"), .Select("low")) Z (
    .D(alu_1_result), .Q(Z_q), .clk(CLK), .clr(RST));  // open: en
  assign \内部总线  = PCout ? PC_q : 32'bz;  // Controlled_Buffer controlled_buffer_4
  assign \内部总线  = DRout ? DR_q : 32'bz;  // Controlled_Buffer controlled_buffer_5
  assign \内部总线  = Zout ? Z_q : 32'bz;  // Controlled_Buffer controlled_buffer_6
  Register #(.width(32), .trigger("rising"), .Select("low")) u_IR (.D(\内部总线 ), .en(IRin), .Q(IR), .clk(CLK), .clr(RST));
  assign \内部总线  = IR_I_out ? bit_extender_1_out : 32'bz;  // Controlled_Buffer controlled_buffer_7
  assign \内部总线  = IR_A_out ? shifter_1_out : 32'bz;  // Controlled_Buffer controlled_buffer_8
  Comparator #(.width(32), .mode("twosComplement")) comparator_1 (
    .a(IR), .b(32'h1000ffff), .eq(comparator_1_eq));  // open: gt, lt
  \微程序控制器  \u_微程序控制器_1  (
    .CLK(CLK), .EQUAL(equal), .mAddr(\微地址_状态 ),
    .ControlBus({IR26out, J, PCout, DRout, Zout, Rout, IR_I_out, IR_A_out, DREout, PCin, ARin, DREin, DRin, Xin, Rin, IRin, PSWin, RegTgt, RegDst, Add, Add4, Slt, READ, Write}),
    .\指令字 (IR), .RST(RST));
  assign \内部总线  = IR26out ? bit_extender_2_out : 32'bz;  // Controlled_Buffer controlled_buffer_9
  // RegisterFile registerfile_1: pin names not known; wires that end beside it: \内部总线 , CLK, Rin, registerfile_1_p4, registerfile_1_p5, registerfile_1_p6
  not not_1 (not_1_out, comparator_1_eq);
  Counter #(.width(12), .max('hfff), .ongoal("wrap"), .trigger("rising"), .behavior("new")) counter_1 (
    .count(not_1_out), .Q(\时钟周期数 ), .clk(CLK), .clr(RST));  // open: load, D, carry, preset, down
  assign bit_extender_1_out = {{16{IR[15]}}, IR[15:0]};  // Bit_Extender bit_extender_1
  assign \内部总线  = Rout ? registerfile_1_p6 : 32'bz;  // Controlled_Buffer controlled_buffer_10
  Multiplexer #(.select(1), .width(5), .disabled("Z"), .enable("false")) multiplexer_1 (
    .in0(IR[25:21]), .in1(IR[20:16]), .out(registerfile_1_p5), .sel(RegTgt));
  Multiplexer #(.select(1), .width(5), .disabled("Z"), .enable("false")) multiplexer_2 (
    .in0(IR[20:16]), .in1(IR[15:11]), .out(registerfile_1_p4), .sel(RegDst));
  Comparator #(.width(5), .mode("twosComplement")) comparator_2 (
    .a(5'b00011), .b(\微地址_状态 ), .eq(comparator_2_eq));  // open: gt, lt
  assign bit_extender_2_out = {{6{1'b0}}, IR[25:0]};  // Bit_Extender bit_extender_2
  Counter #(.width(12), .max('hfff), .ongoal("wrap"), .trigger("rising"), .behavior("old")) counter_2 (
    .count(and_1_out), .Q(\指令数 ), .clk(CLK), .clr(RST));  // open: load, D, carry, preset
  and and_1 (and_1_out, not_1_out, comparator_2_eq);
  Shifter #(.width(32), .shift("ll")) shifter_1 (.in(bit_extender_1_out), .\dist (5'b00010), .out(shifter_1_out));

  // Other names for the same wires on the sheet: rd[4:0] = IR[15:11]; rt[4:0] = IR[20:16]; rs[4:0] = IR[25:21];
  //   控制总线[23:0] = {IR26out, J, PCout, DRout, Zout, Rout, IR_I_out, IR_A_out, DREout, PCin, ARin, DREin, DRin, Xin, Rin, IRin, PSWin, RegTgt, RegDst, Add, Add4, Slt, READ, Write}

  // Notes on the sheet:
  //   MEM
  //   外部总线
  //   内部总线
  //   单总线结构 MIPS 处理器（微程序控制器）数据通路
  //   支持LW、SW、BEQ、SLT、ADDI、ADD、J等7条指令
  //   Immediate32
  //   AddressOffset32
endmodule

module \微程序控制器  (
  input  EQUAL,
  input  [31:0] \指令字 ,
  input  RST,
  input  CLK,
  output [4:0] mAddr,
  output [23:0] ControlBus
);

  wire ADD, ADDI, BEQ, J, LW, not_1_out, Other, P0, P1, P2, SLT, SW;
  wire [1:0] \判别测试逻辑_1_m0 ;
  wire [4:0] multiplexer_1_out, rom_1_data, \微程序入口查找逻辑_测试_1_s0 ;

  \微程序入口查找逻辑_测试  \u_微程序入口查找逻辑_测试_1  (
    .LW(LW), .S4(\微程序入口查找逻辑_测试_1_s0 [4]), .SW(SW), .S3(\微程序入口查找逻辑_测试_1_s0 [3]), .BEQ(BEQ), .SLT(SLT),
    .S2(\微程序入口查找逻辑_测试_1_s0 [2]), .S1(\微程序入口查找逻辑_测试_1_s0 [1]), .ADDI(ADDI), .S0(\微程序入口查找逻辑_测试_1_s0 [0]),
    .ADD(ADD), .J(J));
  \判别测试逻辑  \u_判别测试逻辑_1  (.P0(P0), .P1(P1), .EQUAL(EQUAL), .M1(\判别测试逻辑_1_m0 [1]), .M0(\判别测试逻辑_1_m0 [0]));
  Multiplexer #(.select(2), .width(5), .disabled("Z"), .enable("false")) multiplexer_1 (
    .in0(rom_1_data), .in1(\微程序入口查找逻辑_测试_1_s0 ), .in2(5'b10000), .out(multiplexer_1_out), .sel(\判别测试逻辑_1_m0 ));  // open: in3
  Register #(.width(5), .trigger("rising"), .Select("low")) register_1 (
    .D(multiplexer_1_out), .Q(mAddr), .clk(not_1_out), .clr(RST));  // open: en
  not not_1 (not_1_out, CLK);
  \指令译码器  \u_指令译码器_1  (
    .IR(\指令字 ), .LW(LW), .SW(SW), .BEQ(BEQ), .ADDI(ADDI), .SLT(SLT), .OtherInstr(Other), .ADD(ADD), .J(J));
  ROM #(.addrWidth(5), .dataWidth(32), .Select("high")) rom_1 (
    .addr(mAddr), .data({ControlBus, P0, P1, P2, rom_1_data}));

  // Notes on the sheet:
  //   输入引脚
  //   判别测试逻辑
  //   微程序入口
  //   输出引脚
  //   下址字段
  //   beq分支
  //   微地址寄存器μAR
  //   微程序控制器（下址字段法）
  //   微地址
  //   控制存储器
  //   指令译码器
  //   contents of rom_1 (hex, n*v repeats v):
  //   20240001 802 8500203 10010080 4040005 2001006 8200007 100208 10020000 404000a 200100b 820000c
  //   408400d 800100 404000f 400c040 20040011 1001012 8400000 4040014 4004415 8022000 4040017 2001018
  //   8020000 404001a 400501b 8022000 2004001d c000001e 8400000
  //   控制字段
  //   指令译码信号
  //   微指令
  //   判断逻辑
endmodule

module \指令译码器  (
  input  [31:0] IR,
  output LW,
  output SW,
  output BEQ,
  output ADDI,
  output SLT,
  output OtherInstr,
  output ADD,
  output J
);

  wire comparator_6_eq, comparator_7_eq, comparator_8_eq;

  Comparator #(.width(6), .mode("twosComplement")) comparator_1 (.a(IR[31:26]), .b(6'b000010), .eq(J));  // open: gt, lt
  Comparator #(.width(6), .mode("twosComplement")) comparator_2 (
    .a(IR[31:26]), .b(6'b100011), .eq(LW));  // open: gt, lt
  Comparator #(.width(6), .mode("twosComplement")) comparator_3 (
    .a(IR[31:26]), .b(6'b101011), .eq(SW));  // open: gt, lt
  Comparator #(.width(6), .mode("twosComplement")) comparator_4 (
    .a(IR[31:26]), .b(6'b000100), .eq(BEQ));  // open: gt, lt
  Comparator #(.width(6), .mode("twosComplement")) comparator_5 (
    .a(IR[31:26]), .b(6'b001000), .eq(ADDI));  // open: gt, lt
  Comparator #(.width(6), .mode("twosComplement")) comparator_6 (
    .a(IR[31:26]), .b({6{1'b0}}), .eq(comparator_6_eq));  // open: gt, lt
  Comparator #(.width(6), .mode("twosComplement")) comparator_7 (
    .a(IR[5:0]), .b(6'b101010), .eq(comparator_7_eq));  // open: gt, lt
  Comparator #(.width(6), .mode("twosComplement")) comparator_8 (
    .a(IR[5:0]), .b(6'b100000), .eq(comparator_8_eq));  // open: gt, lt
  and and_1 (SLT, comparator_7_eq, comparator_6_eq);
  and and_2 (ADD, comparator_6_eq, comparator_8_eq);
  nor nor_1 (OtherInstr, J, ADD, BEQ, SW, LW, ADDI, SLT);

  // Other names for the same wires on the sheet: FUNCT[5:0] = IR[5:0]; OP[5:0] = IR[31:26]

  // Notes on the sheet:
  //   输入引脚
  //   指令译码器（ID）
  //   输出引脚
endmodule

// 入口查找
module \微程序入口查找逻辑  (
  input  LW,
  input  SW,
  input  BEQ,
  input  SLT,
  input  ADDI,
  output S4,
  output S3,
  output S2,
  output S1,
  output S0
);

  or or_1 (S4, SLT, ADDI);
  or or_2 (S3, SW, BEQ);
  or or_3 (S2, LW, BEQ, ADDI);
  or or_4 (S1, BEQ, SLT, ADDI);
  or or_5 (S0, SW, SLT);

  // Notes on the sheet:
  //   微程序入口查找逻辑
endmodule

// 测试判断
module \判别测试逻辑  (
  input  P0,
  input  P1,
  input  EQUAL,
  output M1,
  output M0
);

  wire not_1_out;

  not not_1 (not_1_out, P0);
  and and_1 (M1, not_1_out, P1, EQUAL);

  assign M0 = P0;

  // Notes on the sheet:
  //   判别测试逻辑
endmodule

module ALU (
  input  ADD,
  input  ADD4,
  input  [31:0] X,
  input  [31:0] Y,
  input  J,
  input  SLT,
  output Equal,
  output [31:0] Result
);

  wire [0:0] comparator_1_lt;
  wire [1:0] priority_encoder_1_out;
  wire [31:0] adder_1_out, adder_2_out, shifter_1_out, subtractor_1_out;

  Pull_Resistor #(.pull(0)) pull_resistor_1 (.node(Y));
  Adder #(.width(32)) adder_1 (.a(X), .b(Y), .out(adder_1_out));  // open: cin, cout
  Adder #(.width(32)) adder_2 (.a(X), .b(32'h4), .out(adder_2_out));  // open: cin, cout
  Shifter #(.width(32), .shift("ll")) shifter_1 (.in(Y), .\dist (5'b00010), .out(shifter_1_out));
  Subtractor #(.width(32)) subtractor_1 (.a(32'h4), .b(X), .out(subtractor_1_out));  // open: bin, bout
  Comparator #(.width(32), .mode("twosComplement")) comparator_1 (
    .a(X), .b(Y), .eq(Equal), .lt(comparator_1_lt[0]));  // open: gt
  Priority_Encoder #(.select(2), .disabled("Z")) priority_encoder_1 (
    .in0(ADD), .in1(ADD4), .in2(J), .in3(SLT), .out(priority_encoder_1_out));  // open: gs, en_out, en_in
  Pull_Resistor #(.pull(0)) pull_resistor_2 (.node(priority_encoder_1_out));
  Multiplexer #(.select(2), .width(32), .disabled("Z"), .enable("false")) multiplexer_1 (
    .in0(adder_1_out), .in1(adder_2_out), .in2({subtractor_1_out[31:28], shifter_1_out[27:0]}),
    .in3({{31{1'b0}}, comparator_1_lt[0]}), .out(Result), .sel(priority_encoder_1_out));

  // Notes on the sheet:
  //   输入引脚
  //   算术逻辑运算单元ALU
  //   输出引脚
endmodule

module \测试  (
  input  LW,
  input  SW,
  input  BEQ,
  input  SLT,
  input  ADDI,
  input  ADD,
  input  J,
  input  P0,
  input  P1,
  input  EQUAL,
  output [4:0] \微程序入口地址 ,
  output [4:0] out_12,
  output [1:0] M,
  output [1:0] out_14
);

  \判别测试逻辑  \u_判别测试逻辑_1  (.P0(P0), .P1(P1), .EQUAL(EQUAL), .M1(M[1]), .M0(M[0]));
  \判别测试逻辑_测试  \u_判别测试逻辑_测试_1  (.P0(P0), .P1(P1), .EQUAL(EQUAL), .M1(out_14[1]), .M0(out_14[0]));
  \微程序入口查找逻辑  \u_微程序入口查找逻辑_1  (
    .LW(LW), .SW(SW), .BEQ(BEQ), .SLT(SLT), .ADDI(ADDI), .S4(\微程序入口地址 [4]), .S3(\微程序入口地址 [3]),
    .S2(\微程序入口地址 [2]), .S1(\微程序入口地址 [1]), .S0(\微程序入口地址 [0]));
  \微程序入口查找逻辑_测试  \u_微程序入口查找逻辑_测试_1  (
    .LW(LW), .S4(out_12[4]), .SW(SW), .S3(out_12[3]), .BEQ(BEQ), .SLT(SLT), .S2(out_12[2]), .S1(out_12[1]),
    .ADDI(ADDI), .S0(out_12[0]), .ADD(ADD), .J(J));
  // Probe on \微程序入口地址 
  // Probe on out_12
endmodule

// 微程序入口查找逻辑
module \微程序入口查找逻辑_测试  (
  input  LW,
  input  SW,
  input  BEQ,
  input  SLT,
  input  ADDI,
  input  ADD,
  input  J,
  output S4,
  output S3,
  output S2,
  output S1,
  output S0
);

  or or_1 (S4, SLT, ADDI, ADD, J);
  or or_2 (S3, SW, BEQ, ADD, J);
  or or_3 (S2, LW, BEQ, ADDI, J);
  or or_4 (S1, BEQ, SLT, ADDI);
  or or_5 (S0, SW, SLT, ADD);
endmodule

module \判别测试逻辑_测试  (
  input  P0,
  input  P1,
  input  EQUAL,
  output M1,
  output M0
);
endmodule
